// Logisim project cpu.circ as structural Verilog: 6 circuits, main circuit main
module main (
  input  [31:0] RS_READ_VALUE,
  input  [31:0] RT_READ_VALUE,
  input  [31:0] INSTRUCTION,
  input  CLOCK,
  output [31:0] t0,
  output [31:0] t1,
  output [31:0] t2,
  output [31:0] t3,
  output [4:0] RS,
  output [4:0] RT,
  output [4:0] Write_Register,
  output [31:0] RD_WRITE_VALUE,
  output RD_WRITE_ENABLE,
  output [23:0] FETCH_ADDRESS
);

  wire ALU_equal, AluSrc, and_1_out, and_2_out, and_3_out, and_4_out, and_5_out, and_6_out, beq, bne, branch,
       \byte , comparator_1_eq, comparator_2_eq, comparator_3_eq, comparator_4_eq, comparator_5_eq,
       comparator_6_eq, comparator_10_eq, comparator_12_eq, comparator_13_eq, comparator_14_eq,
       comparator_15_eq, comparator_16_eq, comparator_17_eq, comparator_18_eq, comparator_19_eq,
       comparator_20_eq, comparator_21_eq, comparator_22_eq, comparator_23_eq, comparator_24_eq, LED,
       MemToReg, muxie, not_1_out, not_2_out, or_1_out, or_6_out, or_7_out, R_Type, RegDest, store,
       tchecker_1_tcheck, tchecker_2_tcheck, tchecker_3_tcheck, tchecker_4_tcheck, Use_imm, WriteMem,
       WriteReg, x___imm, x___t;
  wire [1:0] tchecker_1_treg, tchecker_2_treg, tchecker_3_treg;
  wire [4:0] multiplexer_6_out;
  wire [5:0] i_type_to_alu_1_func_code, multiplexer_13_out, opcode;
  wire [15:0] address;
  wire [31:0] adder_1_out, adder_2_out, adder_3_out, ALU_result, bit_extender_1_out, bit_extender_2_out,
       bit_extender_3_out, immediate_extender_1_immediate_out, MEM_data_mem_out, multiplexer_1_out,
       multiplexer_2_out, multiplexer_3_out, multiplexer_5_out, multiplexer_10_out, multiplexer_11_out,
       multiplexer_12_out, multiplexer_14_out, multiplexer_15_out, multiplexer_16_out, PC_q,
       RegFile_read_data_1, RegFile_read_data_2, RS_t, RT_t, shifter_1_out, shifter_2_out, subtractor_1_out,
       subtractor_2_out;
  wire [31:24] PC_2_q;

  assign bit_extender_1_out = {{6{1'b0}}, {RS, RT, address}};  // Bit_Extender bit_extender_1
  Subtractor #(.width(32)) subtractor_1 (
    .a(bit_extender_1_out), .b(32'h100000), .out(subtractor_1_out));  // open: bin, bout
  Comparator #(.width(6)) comparator_1 (.a(opcode), .b(6'b000011), .eq(comparator_1_eq));  // open: gt, lt
  Comparator #(.width(6)) comparator_2 (.a(opcode), .b(6'b000010), .eq(comparator_2_eq));  // open: gt, lt
  Comparator #(.width(6)) comparator_3 (.a(opcode), .b({6{1'b0}}), .eq(comparator_3_eq));  // open: gt, lt
  Comparator #(.width(6)) comparator_4 (.a(address[5:0]), .b(6'b001000), .eq(comparator_4_eq));  // open: gt, lt
  Adder #(.width(32)) adder_1 (.a({PC_2_q, FETCH_ADDRESS}), .b(32'h1), .out(adder_1_out));  // open: cin, cout
  Multiplexer #(.width(32)) multiplexer_1 (
    .in0(adder_1_out), .in1(adder_2_out), .out(multiplexer_1_out), .sel(branch));  // open: en
  or or_1 (or_1_out, comparator_1_eq, comparator_2_eq);
  and and_1 (and_1_out, comparator_3_eq, comparator_4_eq);
  Register #(.width(32)) PC (.D(adder_1_out), .Q(PC_q), .clk(CLOCK));  // open: en, clr
  or or_2 (muxie, branch, or_1_out, and_1_out);
  Multiplexer #(.width(32)) multiplexer_2 (
    .in0(multiplexer_1_out), .in1(subtractor_1_out), .out(multiplexer_2_out), .sel(or_1_out));  // open: en
  // Probe on t0
  Multiplexer #(.width(32)) multiplexer_3 (
    .in0(INSTRUCTION), .in1({32{1'b0}}), .out(multiplexer_3_out), .sel(muxie));  // open: en
  Register #(.width(32)) register_1 (
    .D(multiplexer_3_out), .Q({opcode, RS, RT, address}), .clk(CLOCK));  // open: en, clr
  Multiplexer #(.width(32)) multiplexer_4 (
    .in0(multiplexer_16_out), .in1(adder_3_out), .out(RD_WRITE_VALUE), .sel(comparator_5_eq));  // open: en
  Comparator #(.width(6)) comparator_5 (.a(opcode), .b(6'b000011), .eq(comparator_5_eq));  // open: gt, lt
  assign bit_extender_2_out = {{16{address[15]}}, address};  // Bit_Extender bit_extender_2
  Multiplexer #(.width(32)) multiplexer_5 (
    .in0(multiplexer_2_out), .in1(subtractor_2_out), .out(multiplexer_5_out), .sel(and_1_out));  // open: en
  Subtractor #(.width(32)) subtractor_2 (.a(RS_t), .b(32'h100000), .out(subtractor_2_out));  // open: bin, bout
  // Probe on t1
  Adder #(.width(32)) adder_2 (.a(PC_q), .b(bit_extender_2_out), .out(adder_2_out));  // open: cin, cout
  Register #(.width(32)) PC_2 (.D(multiplexer_5_out), .Q({PC_2_q, FETCH_ADDRESS}), .clk(CLOCK));  // open: en, clr
  // Probe on t2
  Adder #(.width(32)) adder_3 (.a(32'h100000), .b({PC_2_q, FETCH_ADDRESS}), .out(adder_3_out));  // open: cin, cout
  // Probe on t3
  Comparator #(.width(6)) comparator_6 (.a(opcode), .b(6'b000011), .eq(comparator_6_eq));  // open: gt, lt
  Multiplexer #(.width(5)) multiplexer_6 (
    .in0(RT), .in1(address[15:11]), .out(multiplexer_6_out), .sel(RegDest));  // open: en
  TChecker tchecker_1 (.in_1(RS), .TCheck(tchecker_1_tcheck), .TReg(tchecker_1_treg));
  TChecker tchecker_2 (.in_1(RT), .TCheck(tchecker_2_tcheck), .TReg(tchecker_2_treg));
  Multiplexer #(.width(5)) multiplexer_7 (
    .in0(multiplexer_6_out), .in1({5{1'b1}}), .out(Write_Register), .sel(comparator_6_eq));  // open: en
  TChecker tchecker_3 (.in_1(multiplexer_6_out), .TCheck(tchecker_3_tcheck), .TReg(tchecker_3_treg));
  Comparator #(.width(6)) comparator_7 (.a(6'b000101), .b(opcode), .eq(bne));  // open: gt, lt
  Comparator #(.width(6)) comparator_8 (.a(6'b000100), .b(opcode), .eq(beq));  // open: gt, lt
  Comparator #(.width(6)) comparator_9 (.a({6{1'b0}}), .b(opcode), .eq(R_Type));  // open: gt, lt
  Use_Immediate use_immediate_1 (.in_1(opcode), .in_2(address[5:0]), .Operation(Use_imm));
  TChecker tchecker_4 (.in_1(address[15:11]), .TCheck(tchecker_4_tcheck));  // open: TReg
  and and_2 (and_2_out, R_Type, LED);
  LED led_1 (.in(and_2_out));
  and and_3 (and_3_out, store, not_1_out);
  not not_1 (not_1_out, tchecker_4_tcheck);
  Comparator #(.width(6)) comparator_10 (.a(opcode), .b(6'b000011), .eq(comparator_10_eq));  // open: gt, lt
  regfile_main RegFile (
    .Read_register_1(tchecker_1_treg), .Read_register_2(tchecker_2_treg), .write_register(tchecker_3_treg),
    .write_data(multiplexer_16_out), .t0_Value(t0), .t1_Value(t1), .t2_Value(t2), .t3_Value(t3),
    .RegWrite(and_4_out), .clock(CLOCK), .Read_Data_1(RegFile_read_data_1), .Read_Data_2(RegFile_read_data_2));
  and and_4 (and_4_out, store, tchecker_3_tcheck);
  or or_3 (RD_WRITE_ENABLE, and_3_out, comparator_10_eq);
  Immediate_Extender immediate_extender_1 (
    .opcode_in(opcode), .immediate_in(address), .shift_amount(address[10:6]),
    .immediate_out(immediate_extender_1_immediate_out));
  Comparator #(.width(6)) comparator_11 (.a(6'b001111), .b(opcode), .eq(x___imm));  // open: gt, lt
  Comparator #(.width(6)) comparator_12 (.a(6'b100100), .b(opcode), .eq(comparator_12_eq));  // open: gt, lt
  Comparator #(.width(6)) comparator_13 (.a(6'b100000), .b(opcode), .eq(comparator_13_eq));  // open: gt, lt
  Multiplexer #(.width(32)) multiplexer_8 (
    .in0(RT_READ_VALUE), .in1(RegFile_read_data_2), .out(RT_t), .sel(tchecker_2_tcheck));  // open: en
  or or_4 (\byte , comparator_12_eq, comparator_13_eq);
  assign bit_extender_3_out = {{16{1'b0}}, address};  // Bit_Extender bit_extender_3
  Multiplexer #(.width(32)) multiplexer_9 (
    .in0(RS_READ_VALUE), .in1(RegFile_read_data_1), .out(RS_t), .sel(tchecker_1_tcheck));  // open: en
  Multiplexer #(.width(32)) multiplexer_10 (.in0(RS_t), .in1(RT_t), .out(multiplexer_10_out), .sel(x___t));  // open: en
  Multiplexer #(.width(32)) multiplexer_11 (
    .in0(RT_t), .in1(immediate_extender_1_immediate_out), .out(multiplexer_11_out), .sel(Use_imm));  // open: en
  Multiplexer #(.width(32)) multiplexer_12 (
    .in0(multiplexer_10_out), .in1(bit_extender_3_out), .out(multiplexer_12_out), .sel(x___imm));  // open: en
  I_type_to_ALU i_type_to_alu_1 (.opcode(opcode), .Func_Code(i_type_to_alu_1_func_code));
  control control_1 (
    .OPcode(opcode), .RegDst(RegDest), .ALUSrc(AluSrc), .MemToReg(MemToReg), .WriteReg(WriteReg),
    .WriteMem(WriteMem));  // open: ReadMem
  alu_main ALU (
    .Switch__S(multiplexer_13_out), .X(multiplexer_12_out), .Equal(ALU_equal), .RESULT(ALU_result),
    .Signed_Overflow(LED), .Y(multiplexer_11_out));
  Multiplexer #(.width(6)) multiplexer_13 (
    .in0(i_type_to_alu_1_func_code), .in1(address[5:0]), .out(multiplexer_13_out), .sel(R_Type));  // open: en
  not not_2 (not_2_out, ALU_equal);
  and and_5 (and_5_out, not_2_out, bne);
  Comparator #(.width(6)) comparator_14 (.a(6'b100000), .b(opcode), .eq(comparator_14_eq));  // open: gt, lt
  Comparator #(.width(6)) comparator_15 (.a(6'b001101), .b(opcode), .eq(comparator_15_eq));  // open: gt, lt
  Comparator #(.width(6)) comparator_16 (.a(6'b001100), .b(opcode), .eq(comparator_16_eq));  // open: gt, lt
  Comparator #(.width(6)) comparator_17 (.a(6'b001000), .b(opcode), .eq(comparator_17_eq));  // open: gt, lt
  Comparator #(.width(6)) comparator_18 (.a(6'b001001), .b(opcode), .eq(comparator_18_eq));  // open: gt, lt
  Comparator #(.width(6)) comparator_19 (.a(opcode), .b(6'b100100), .eq(comparator_19_eq));  // open: gt, lt
  Comparator #(.width(6)) comparator_20 (.a({6{1'b0}}), .b(address[5:0]), .eq(comparator_20_eq));  // open: gt, lt
  Comparator #(.width(6)) comparator_21 (.a(6'b000010), .b(address[5:0]), .eq(comparator_21_eq));  // open: gt, lt
  Comparator #(.width(6)) comparator_22 (.a(6'b000011), .b(address[5:0]), .eq(comparator_22_eq));  // open: gt, lt
  and and_6 (and_6_out, ALU_equal, beq);
  or or_5 (branch, and_5_out, and_6_out);
  mem_main MEM (
    .Data_Mem_Addr(ALU_result), .Data_Mem_In(RT_t), .ACCESS_BYTE(\byte ), .MEM_WRITE(WriteMem),
    .CLOCK(CLOCK), .Data_Mem_Out(MEM_data_mem_out));
  Shifter #(.width(32)) shifter_1 (.in(MEM_data_mem_out), .\dist (5'b11000), .out(shifter_1_out));
  or or_6 (or_6_out, comparator_14_eq, comparator_15_eq, comparator_16_eq, comparator_17_eq, comparator_18_eq, comparator_19_eq);
  or or_7 (or_7_out, comparator_20_eq, comparator_21_eq, comparator_22_eq);
  Multiplexer #(.width(32)) multiplexer_14 (
    .in0(MEM_data_mem_out), .in1(shifter_2_out), .out(multiplexer_14_out), .sel(comparator_24_eq));  // open: en
  Shifter #(.width(32), .shift("ar")) shifter_2 (.in(shifter_1_out), .\dist (5'b11000), .out(shifter_2_out));
  Comparator #(.width(6)) comparator_23 (.a({6{1'b0}}), .b(opcode), .eq(comparator_23_eq));  // open: gt, lt
  and and_7 (x___t, comparator_23_eq, or_7_out);
  Multiplexer #(.width(32)) multiplexer_15 (
    .in0(MEM_data_mem_out), .in1(multiplexer_14_out), .out(multiplexer_15_out), .sel(\byte ));  // open: en
  or or_8 (store, WriteReg, or_6_out);
  Multiplexer #(.width(32)) multiplexer_16 (
    .in0(ALU_result), .in1(multiplexer_15_out), .out(multiplexer_16_out), .sel(MemToReg));  // open: en
  Comparator #(.width(6)) comparator_24 (.a(opcode), .b(6'b100000), .eq(comparator_24_eq));  // open: gt, lt

  // Other names for the same wires on the sheet: function[5:0] = address[5:0]; immediate[15:0] = address;
  //   word_addressed_target[23:0] = {RS[2:0], RT, address}; shift_amount[4:0] = address[10:6];
  //   register_d[4:0] = address[15:11]; address[25:16] = {RS, RT}; register_t[4:0] = RT; register_s[4:0] = RS;
  //   clk = CLOCK; RD_Write[31:0] = RD_WRITE_VALUE; RD_Write_E = RD_WRITE_ENABLE; S[31:0] = RS_READ_VALUE;
  //   store_register[4:0] = Write_Register; T[31:0] = RT_READ_VALUE

  // Notes on the sheet:
  //   These are outputs/inputs from run.circ
  //   Take a branch?
  //   CLOCK POOP
  //   Take a jump?
  //   Muxie = 1 if using noop
  //   These are outputs to run.circ
  //   Instruction Diversification
  //   JR logic
  //   LED logic
  //   Take the branch?
  //   Checks for r-type instruction
  //   Do we need the immediate or naw?
  //   Enable RD Write?
  //   Register Logic
  //   Do we use immediate as x input to ALU
  //   Do we take take the byte from memory
  //   ALU input logic
  //   HELPER JUNKYARD LOGIC
  //   Sad Attempt at a Control
  //   Memory Logic
  //   Access Byte Logic
  //   Do we store output?
  //   Do we use RT as x input to ALU?
  //   Write output to a register logic
endmodule

module control (
  input  [5:0] OPcode,
  output RegDst,
  output ALUSrc,
  output MemToReg,
  output WriteReg,
  output ReadMem,
  output WriteMem
);

  wire and_4_out, and_5_out, and_6_out, and_7_out, not_1_out, not_2_out, not_3_out, not_4_out, not_5_out,
       not_6_out, not_7_out, not_8_out, not_9_out, not_10_out, not_11_out, not_12_out, not_13_out,
       not_14_out, not_15_out, not_16_out, not_17_out, not_18_out, not_19_out, not_20_out, not_21_out,
       not_22_out, not_23_out, not_24_out, not_25_out, not_26_out, not_27_out;

  not not_1 (not_1_out, OPcode[2]);
  not not_2 (not_2_out, OPcode[0]);
  not not_3 (not_3_out, OPcode[1]);
  not not_4 (not_4_out, OPcode[5]);
  not not_5 (not_5_out, OPcode[4]);
  not not_6 (not_6_out, OPcode[3]);
  and and_1 (RegDst, not_4_out, not_5_out, not_6_out, not_1_out, not_3_out, not_2_out);
  not not_7 (not_7_out, OPcode[2]);
  not not_8 (not_8_out, OPcode[3]);
  not not_9 (not_9_out, OPcode[4]);
  and and_2 (ReadMem, OPcode[5], not_9_out, not_8_out, not_7_out, OPcode[1], OPcode[0]);
  not not_10 (not_10_out, OPcode[4]);
  not not_11 (not_11_out, OPcode[2]);
  and and_3 (WriteMem, OPcode[5], not_10_out, OPcode[3], not_11_out, OPcode[1], OPcode[0]);
  not not_12 (not_12_out, OPcode[0]);
  not not_13 (not_13_out, OPcode[3]);
  not not_14 (not_14_out, OPcode[4]);
  not not_15 (not_15_out, OPcode[5]);
  not not_16 (not_16_out, OPcode[1]);
  and and_4 (and_4_out, not_15_out, not_14_out, not_13_out, OPcode[2], not_16_out, not_12_out);
  not not_17 (not_17_out, OPcode[5]);
  not not_18 (not_18_out, OPcode[4]);
  and and_5 (and_5_out, not_17_out, not_18_out, OPcode[3], OPcode[2], OPcode[1], OPcode[0]);
  or or_1 (ALUSrc, ReadMem, WriteMem);
  or or_2 (WriteReg, RegDst, and_5_out, ReadMem);
  not not_19 (not_19_out, OPcode[0]);
  not not_20 (not_20_out, OPcode[4]);
  not not_21 (not_21_out, OPcode[2]);
  not not_22 (not_22_out, OPcode[3]);
  not not_23 (not_23_out, OPcode[1]);
  and and_6 (and_6_out, OPcode[5], not_20_out, not_22_out, not_21_out, not_23_out, not_19_out);
  not not_24 (not_24_out, OPcode[3]);
  not not_25 (not_25_out, OPcode[0]);
  not not_26 (not_26_out, OPcode[1]);
  not not_27 (not_27_out, OPcode[4]);
  and and_7 (and_7_out, OPcode[5], not_27_out, not_24_out, OPcode[2], not_26_out, not_25_out);
  or or_3 (MemToReg, and_6_out, ReadMem, and_7_out);
endmodule

module Immediate_Extender (
  input  [5:0] opcode_in,
  input  [4:0] shift_amount,
  input  [15:0] immediate_in,
  output [31:0] immediate_out
);

  wire comparator_1_eq, comparator_2_eq, comparator_3_eq, comparator_4_eq;
  wire [1:0] or_1_out;
  wire [31:0] bit_extender_1_out, bit_extender_2_out, bit_extender_3_out, bit_extender_4_out,
       multiplexer_1_out, multiplexer_2_out;

  Comparator #(.width(6)) comparator_1 (.a(opcode_in), .b(6'b001000), .eq(comparator_1_eq));  // open: gt, lt
  Comparator #(.width(6)) comparator_2 (.a(opcode_in), .b(6'b001001), .eq(comparator_2_eq));  // open: gt, lt
  Comparator #(.width(6)) comparator_3 (.a(opcode_in), .b(6'b001101), .eq(comparator_3_eq));  // open: gt, lt
  Comparator #(.width(6)) comparator_4 (.a(opcode_in), .b(6'b001111), .eq(comparator_4_eq));  // open: gt, lt
  Comparator #(.width(6)) comparator_5 (.a(opcode_in), .b({6{1'b0}}), .eq(or_1_out[1]));  // open: gt, lt
  or or_1 (or_1_out[0], comparator_1_eq, comparator_2_eq, comparator_3_eq);
  assign bit_extender_1_out = {{16{immediate_in[15]}}, immediate_in};  // Bit_Extender bit_extender_1
  assign bit_extender_2_out = {{16{1'b0}}, immediate_in};  // Bit_Extender bit_extender_2
  assign bit_extender_3_out = {{16{1'b0}}, immediate_in};  // Bit_Extender bit_extender_3
  Multiplexer #(.width(32)) multiplexer_1 (
    .in0(bit_extender_1_out), .in1(bit_extender_2_out), .out(multiplexer_1_out), .sel(comparator_3_eq));  // open: en
  assign bit_extender_4_out = {{27{1'b0}}, shift_amount};  // Bit_Extender bit_extender_4
  Multiplexer #(.width(32)) multiplexer_2 (
    .in0(bit_extender_3_out), .in1(32'h10), .out(multiplexer_2_out), .sel(comparator_4_eq));  // open: en
  Multiplexer #(.select(2), .width(32)) multiplexer_3 (
    .in0(multiplexer_2_out), .in1(multiplexer_1_out), .in2(bit_extender_4_out), .out(immediate_out),
    .sel(or_1_out));  // open: in3, en
endmodule

module TChecker (
  input  [4:0] in_1,
  output TCheck,
  output [1:0] TReg
);

  wire comparator_1_lt, comparator_2_gt;
  wire [4:2] subtractor_1_out;

  Comparator #(.width(5), .mode("unsigned")) comparator_1 (
    .a(in_1), .b(5'b01100), .lt(comparator_1_lt));  // open: gt, eq
  Comparator #(.width(5)) comparator_2 (.a(in_1), .b(5'b00111), .gt(comparator_2_gt));  // open: eq, lt
  Subtractor #(.width(5)) subtractor_1 (.a(in_1), .b(5'b01000), .out({subtractor_1_out, TReg}));  // open: bin, bout
  and and_1 (TCheck, comparator_1_lt, comparator_2_gt);
endmodule

module Use_Immediate (
  input  [5:0] in_1,
  input  [5:0] in_2,
  output Operation
);

  wire and_1_out, and_2_out, and_3_out, comparator_1_eq, comparator_2_eq, comparator_3_eq, comparator_4_eq,
       comparator_5_eq, comparator_6_eq, comparator_7_eq, comparator_8_eq, comparator_9_eq, comparator_10_eq,
       comparator_11_eq, comparator_12_eq, comparator_13_eq, or_1_out;

  Comparator #(.width(6)) comparator_1 (.a(in_1), .b({6{1'b0}}), .eq(comparator_1_eq));  // open: gt, lt
  Comparator #(.width(6)) comparator_2 (.a(in_1), .b(6'b001000), .eq(comparator_2_eq));  // open: gt, lt
  Comparator #(.width(6)) comparator_3 (.a(in_1), .b(6'b001001), .eq(comparator_3_eq));  // open: gt, lt
  Comparator #(.width(6)) comparator_4 (.a(in_1), .b(6'b001101), .eq(comparator_4_eq));  // open: gt, lt
  Comparator #(.width(6)) comparator_5 (.a(in_1), .b(6'b001111), .eq(comparator_5_eq));  // open: gt, lt
  Comparator #(.width(6)) comparator_6 (.a(in_1), .b(6'b100011), .eq(comparator_6_eq));  // open: gt, lt
  Comparator #(.width(6)) comparator_7 (.a(in_1), .b(6'b100100), .eq(comparator_7_eq));  // open: gt, lt
  Comparator #(.width(6)) comparator_8 (.a(in_1), .b(6'b100000), .eq(comparator_8_eq));  // open: gt, lt
  Comparator #(.width(6)) comparator_9 (.a(in_1), .b(6'b101011), .eq(comparator_9_eq));  // open: gt, lt
  Comparator #(.width(6)) comparator_10 (.a(in_1), .b(6'b001100), .eq(comparator_10_eq));  // open: gt, lt
  Comparator #(.width(6)) comparator_11 (.a(in_2), .b({6{1'b0}}), .eq(comparator_11_eq));  // open: gt, lt
  Comparator #(.width(6)) comparator_12 (.a(in_2), .b(6'b000010), .eq(comparator_12_eq));  // open: gt, lt
  Comparator #(.width(6)) comparator_13 (.a(in_2), .b(6'b000011), .eq(comparator_13_eq));  // open: gt, lt
  and and_1 (and_1_out, comparator_11_eq, comparator_1_eq);
  and and_2 (and_2_out, comparator_1_eq, comparator_12_eq);
  and and_3 (and_3_out, comparator_1_eq, comparator_13_eq);
  or or_1 (or_1_out, comparator_9_eq, comparator_10_eq);
  or or_2 (Operation, comparator_6_eq, comparator_7_eq, comparator_8_eq, and_1_out, and_2_out, and_3_out, comparator_2_eq, comparator_3_eq, comparator_4_eq, comparator_5_eq, or_1_out);
endmodule

module I_type_to_ALU (
  input  [5:0] opcode,
  output [5:0] Func_Code
);

  Multiplexer #(.select(5), .width(6)) multiplexer_1 (
    .in0(6'b100001), .in3(6'b100001), .in4(6'b100001), .in8(6'b100000), .in9(6'b100001), .in11(6'b100001),
    .in12(6'b100100), .in13(6'b100101), .in15({6{1'b0}}), .out(Func_Code), .sel(opcode[4:0]));  // open: in1, in2, in5, in6, in7, in10, in14, in16, in17, in18, in19, in20, in21, in22, in23, in24, in25, in26, in27, in28, in29, in30, in31, en
endmodule
